// Logisim project sqrt2.circ as structural Verilog: 25 circuits, main circuit main
module main (
  input  ENABLE,
  input  [15:0] IO_DATA_IN,
  output NAN,
  output PINF,
  output NINF,
  output RESULT,
  output [15:0] IO_DATA_OUT
);

  wire CLK_out;

  Clock CLK (.out(CLK_out));
  sqrt sqrt_1 (
    .CLK(CLK_out), .ENABLE(ENABLE), .IO_DATA_IN(IO_DATA_IN), .IS_NAN(NAN), .IS_PINF(PINF), .IS_NINF(NINF),
    .RESULT(RESULT), .IO_DATA_OUT(IO_DATA_OUT));
endmodule

module sqrt (
  input  CLK,
  input  ENABLE,
  input  [15:0] IO_DATA_IN,
  output IS_NAN,
  output IS_PINF,
  output IS_NINF,
  output RESULT,
  output [15:0] IO_DATA_OUT
);

  wire not_1_out, or_1_out;
  wire [5:0] counter_1_out_4;

  not not_1 (not_1_out, ENABLE);
  or or_1 (or_1_out, RESULT, not_1_out);
  // Probe on counter_1_out_4
  Counter counter_1 (.Enabled(ENABLE), .CLK(CLK), .Done(or_1_out), .out_4(counter_1_out_4));

  assign IO_DATA_OUT = IO_DATA_IN;
endmodule

module JK (
  input  K,
  input  C,
  input  J,
  input  Enabled,
  output Q,
  output NQ
);

  wire and_1_out, and_2_out, not_1_out, rs_1_nq, rs_1_q;

  and and_1 (and_1_out, Q, K);
  and and_2 (and_2_out, J, NQ);
  RS rs_1 (.R(and_1_out), .C(C), .S(and_2_out), .Enabled(Enabled), .Q(rs_1_q), .NQ(rs_1_nq));
  not not_1 (not_1_out, C);
  RS rs_2 (.R(rs_1_nq), .C(not_1_out), .S(rs_1_q), .Enabled(Enabled), .Q(Q), .NQ(NQ));
endmodule

module RS (
  input  R,
  input  C,
  input  S,
  input  Enabled,
  output Q,
  output NQ
);

  wire and_1_out, and_2_out, nand_4_out, not_1_out, not_2_out, por_1_out, transmission_1_p4,
       transmission_2_p4, transmission_3_p3, transmission_3_p5, transmission_4_p3, transmission_4_p5;

  and and_1 (and_1_out, R, Enabled);
  not not_1 (not_1_out, Enabled);
  and and_2 (and_2_out, S, Enabled);
  not not_2 (not_2_out, Enabled);
  // Transmission_Gate transmission_1: pin names not known; wires that end beside it: and_1_out, not_2_out, Enabled, transmission_1_p4
  // Transmission_Gate transmission_2: pin names not known; wires that end beside it: and_2_out, not_1_out, Enabled, transmission_2_p4
  // Transmission_Gate transmission_3: pin names not known; wires that end beside it: 1'b0, Enabled, transmission_3_p3, transmission_1_p4, transmission_3_p5
  not not_3 (transmission_3_p3, Enabled);
  // Transmission_Gate transmission_4: pin names not known; wires that end beside it: 1'b1, Enabled, transmission_4_p3, transmission_2_p4, transmission_4_p5
  not not_4 (transmission_4_p3, Enabled);
  nand nand_1 (transmission_3_p5, transmission_1_p4, C);
  nand nand_2 (transmission_4_p5, C, transmission_2_p4);
  POR por_1 (.out(por_1_out));
  nand nand_3 (Q, transmission_3_p5, NQ);
  nand nand_4 (nand_4_out, Q, transmission_4_p5);
  or or_1 (NQ, nand_4_out, por_1_out);
endmodule

module Dtrigger1 (
  input  D,
  input  C,
  input  Enabled,
  output Q,
  output NQ
);

  wire not_1_out;

  not not_1 (not_1_out, D);
  JK jk_1 (.K(not_1_out), .C(C), .J(D), .Enabled(Enabled), .Q(Q), .NQ(NQ));
endmodule

module DTrigger2 (
  input  [1:0] D,
  input  C,
  input  Enabled,
  output [1:0] out_4,
  output [1:0] out_5
);

  Dtrigger1 dtrigger1_1 (.D(D[0]), .C(C), .Enabled(Enabled), .Q(out_4[0]), .NQ(out_5[0]));
  Dtrigger1 dtrigger1_2 (.D(D[1]), .C(C), .Enabled(Enabled), .Q(out_4[1]), .NQ(out_5[1]));
endmodule

module DTrigger4 (
  input  [3:0] D,
  input  C,
  input  Enabled,
  output [3:0] out_4,
  output [3:0] out_5
);

  DTrigger2 dtrigger2_1 (.D(D[1:0]), .C(C), .Enabled(Enabled), .out_4(out_4[1:0]), .out_5(out_5[1:0]));
  DTrigger2 dtrigger2_2 (.D(D[3:2]), .C(C), .Enabled(Enabled), .out_4(out_4[3:2]), .out_5(out_5[3:2]));
endmodule

module DTrigger8 (
  input  [7:0] D,
  input  C,
  input  Enabled,
  output [7:0] out_4,
  output [7:0] out_5
);

  DTrigger4 dtrigger4_1 (.D(D[3:0]), .C(C), .Enabled(Enabled), .out_4(out_4[3:0]), .out_5(out_5[3:0]));
  DTrigger4 dtrigger4_2 (.D(D[7:4]), .C(C), .Enabled(Enabled), .out_4(out_4[7:4]), .out_5(out_5[7:4]));
endmodule

module DTrigger16 (
  input  [15:0] D,
  input  C,
  input  Enabled,
  output [15:0] out_4,
  output [15:0] out_5
);

  DTrigger8 dtrigger8_1 (.D(D[7:0]), .C(C), .Enabled(Enabled), .out_4(out_4[7:0]), .out_5(out_5[7:0]));
  DTrigger8 dtrigger8_2 (.D(D[15:8]), .C(C), .Enabled(Enabled), .out_4(out_4[15:8]), .out_5(out_5[15:8]));
endmodule

module DTrigger32 (
  input  [31:0] D,
  input  C,
  input  Enabled,
  output [31:0] out_4,
  output [31:0] out_5
);

  DTrigger16 dtrigger16_1 (.D(D[15:0]), .C(C), .Enabled(Enabled), .out_4(out_4[15:0]), .out_5(out_5[15:0]));
  DTrigger16 dtrigger16_2 (.D(D[31:16]), .C(C), .Enabled(Enabled), .out_4(out_4[31:16]), .out_5(out_5[31:16]));
endmodule

module SUM1 (
  input  A,
  input  B,
  input  Cin,
  output S,
  output Cout
);

  wire and_1_out, and_2_out, xor_1_out;

  xor xor_1 (xor_1_out, A, B);
  xor xor_2 (S, xor_1_out, Cin);
  and and_1 (and_1_out, xor_1_out, Cin);
  and and_2 (and_2_out, A, B);
  or or_1 (Cout, and_1_out, and_2_out);
endmodule

module SUM2 (
  input  [1:0] A,
  input  [1:0] B,
  input  Cin,
  output [1:0] S,
  output Cout
);

  wire sum1_1_cout;

  SUM1 sum1_1 (.A(A[0]), .B(B[0]), .Cin(Cin), .S(S[0]), .Cout(sum1_1_cout));
  SUM1 sum1_2 (.A(A[1]), .B(B[1]), .Cin(sum1_1_cout), .S(S[1]), .Cout(Cout));
endmodule

module SUM4 (
  input  [3:0] A,
  input  [3:0] B,
  input  Cin,
  output [3:0] S,
  output Cout
);

  wire sum2_1_cout;

  SUM2 sum2_1 (.A(A[1:0]), .B(B[1:0]), .Cin(Cin), .S(S[1:0]), .Cout(sum2_1_cout));
  SUM2 sum2_2 (.A(A[3:2]), .B(B[3:2]), .Cin(sum2_1_cout), .S(S[3:2]), .Cout(Cout));
endmodule

module SUM8 (
  input  [7:0] A,
  input  [7:0] B,
  input  Cin,
  output [7:0] S,
  output Cout
);

  wire sum4_1_cout;

  SUM4 sum4_1 (.A(A[3:0]), .B(B[3:0]), .Cin(Cin), .S(S[3:0]), .Cout(sum4_1_cout));
  SUM4 sum4_2 (.A(A[7:4]), .B(B[7:4]), .Cin(sum4_1_cout), .S(S[7:4]), .Cout(Cout));
endmodule

module SUM16 (
  input  [15:0] A,
  input  [15:0] B,
  input  Cin,
  output [15:0] S,
  output Cout
);

  wire sum8_1_cout;

  SUM8 sum8_1 (.A(A[7:0]), .B(B[7:0]), .Cin(Cin), .S(S[7:0]), .Cout(sum8_1_cout));
  SUM8 sum8_2 (.A(A[15:8]), .B(B[15:8]), .Cin(sum8_1_cout), .S(S[15:8]), .Cout(Cout));
endmodule

module SUM32 (
  input  [31:0] A,
  input  [31:0] B,
  input  Cin,
  output [31:0] S,
  output Cout
);

  wire sum16_1_cout;

  SUM16 sum16_1 (.A(A[15:0]), .B(B[15:0]), .Cin(Cin), .S(S[15:0]), .Cout(sum16_1_cout));
  SUM16 sum16_2 (.A(A[31:16]), .B(B[31:16]), .Cin(sum16_1_cout), .S(S[31:16]), .Cout(Cout));
endmodule

module Counter (
  input  Enabled,
  input  CLK,
  input  Done,
  output [5:0] out_4
);

  wire and_1_out, not_1_out;

  and and_1 (and_1_out, CLK, not_1_out);
  not not_1 (not_1_out, Done);
  T t_1 (.CLK(and_1_out), .Enabled(Enabled), .Tick(out_4[5]));
  T t_2 (.CLK(out_4[5]), .Enabled(Enabled), .Tick(out_4[4]));
  T t_3 (.CLK(out_4[4]), .Enabled(Enabled), .Tick(out_4[3]));
  T t_4 (.CLK(out_4[3]), .Enabled(Enabled), .Tick(out_4[2]));
  T t_5 (.CLK(out_4[2]), .Enabled(Enabled), .Tick(out_4[1]));
  T t_6 (.CLK(out_4[1]), .Enabled(Enabled), .Tick(out_4[0]));
endmodule

module T (
  input  CLK,
  input  Enabled,
  output Tick
);

  wire dtrigger1_1_nq;

  Dtrigger1 dtrigger1_1 (.D(dtrigger1_1_nq), .C(CLK), .Enabled(Enabled), .Q(Tick), .NQ(dtrigger1_1_nq));
endmodule

module MINUS32 (
  input  [31:0] A,
  input  [31:0] B,
  output [31:0] S,
  output Cout
);

  wire [31:0] sum32_1_s, xor_1_out;

  assign xor_1_out = {32{1'b1}} ^ B;  // XOR_Gate xor_1, 32 bits wide
  // Probe on xor_1_out
  SUM32 sum32_1 (.A(32'h1), .B(xor_1_out), .S(sum32_1_s));  // open: Cin, Cout
  // Probe on sum32_1_s
  SUM32 sum32_2 (.A(A), .B(sum32_1_s), .S(S), .Cout(Cout));  // open: Cin
endmodule

module COMP1 (
  input  A,
  input  B,
  output EQ,
  output MORE,
  output LESS
);

  wire not_1_out, not_2_out, not_3_out, not_4_out;

  xnor xnor_1 (EQ, A, B);
  not not_1 (not_1_out, EQ);
  not not_2 (not_2_out, B);
  not not_3 (not_3_out, EQ);
  not not_4 (not_4_out, A);
  and and_1 (MORE, not_1_out, not_2_out);
  and and_2 (LESS, not_3_out, not_4_out);
endmodule

module COMP2 (
  input  [1:0] A,
  input  [1:0] B,
  output EQ,
  output MORE,
  output LESS
);

  wire and_2_out, and_3_out, comp1_1_eq, comp1_1_less, comp1_1_more, comp1_2_eq, comp1_2_less, comp1_2_more;

  COMP1 comp1_1 (.A(A[1]), .B(B[1]), .EQ(comp1_1_eq), .MORE(comp1_1_more), .LESS(comp1_1_less));
  COMP1 comp1_2 (.A(A[0]), .B(B[0]), .EQ(comp1_2_eq), .MORE(comp1_2_more), .LESS(comp1_2_less));
  and and_1 (EQ, comp1_1_eq, comp1_2_eq);
  and and_2 (and_2_out, comp1_1_eq, comp1_2_more);
  or or_1 (MORE, comp1_1_more, and_2_out);
  or or_2 (LESS, comp1_1_less, and_3_out);
  and and_3 (and_3_out, comp1_1_eq, comp1_2_less);
endmodule

module COMP4 (
  input  [3:0] A,
  input  [3:0] B,
  output EQ,
  output MORE,
  output LESS
);

  wire and_2_out, and_3_out, comp2_1_eq, comp2_1_less, comp2_1_more, comp2_2_eq, comp2_2_less, comp2_2_more;

  COMP2 comp2_1 (.A(A[3:2]), .B(B[3:2]), .EQ(comp2_1_eq), .MORE(comp2_1_more), .LESS(comp2_1_less));
  COMP2 comp2_2 (.A(A[1:0]), .B(B[1:0]), .EQ(comp2_2_eq), .MORE(comp2_2_more), .LESS(comp2_2_less));
  and and_1 (EQ, comp2_1_eq, comp2_2_eq);
  and and_2 (and_2_out, comp2_1_eq, comp2_2_more);
  or or_1 (MORE, comp2_1_more, and_2_out);
  or or_2 (LESS, comp2_1_less, and_3_out);
  and and_3 (and_3_out, comp2_1_eq, comp2_2_less);
endmodule

module COMP8 (
  input  [7:0] A,
  input  [7:0] B,
  output EQ,
  output MORE,
  output LESS
);

  wire and_2_out, and_3_out, comp4_1_eq, comp4_1_less, comp4_1_more, comp4_2_eq, comp4_2_less, comp4_2_more;

  COMP4 comp4_1 (.A(A[7:4]), .B(B[7:4]), .EQ(comp4_1_eq), .MORE(comp4_1_more), .LESS(comp4_1_less));
  COMP4 comp4_2 (.A(A[3:0]), .B(B[3:0]), .EQ(comp4_2_eq), .MORE(comp4_2_more), .LESS(comp4_2_less));
  and and_1 (EQ, comp4_1_eq, comp4_2_eq);
  and and_2 (and_2_out, comp4_1_eq, comp4_2_more);
  or or_1 (MORE, comp4_1_more, and_2_out);
  or or_2 (LESS, comp4_1_less, and_3_out);
  and and_3 (and_3_out, comp4_1_eq, comp4_2_less);
endmodule

module COMP16 (
  input  [15:0] A,
  input  [15:0] B,
  output EQ,
  output MORE,
  output LESS
);

  wire and_2_out, and_3_out, comp8_1_eq, comp8_1_less, comp8_1_more, comp8_2_eq, comp8_2_less, comp8_2_more;

  COMP8 comp8_1 (.A(A[15:8]), .B(B[15:8]), .EQ(comp8_1_eq), .MORE(comp8_1_more), .LESS(comp8_1_less));
  COMP8 comp8_2 (.A(A[7:0]), .B(B[7:0]), .EQ(comp8_2_eq), .MORE(comp8_2_more), .LESS(comp8_2_less));
  and and_1 (EQ, comp8_1_eq, comp8_2_eq);
  and and_2 (and_2_out, comp8_1_eq, comp8_2_more);
  or or_1 (MORE, comp8_1_more, and_2_out);
  or or_2 (LESS, comp8_1_less, and_3_out);
  and and_3 (and_3_out, comp8_1_eq, comp8_2_less);
endmodule

module COMP32 (
  input  [31:0] A,
  input  [31:0] B,
  output EQ,
  output MORE,
  output LESS
);

  wire and_2_out, and_3_out, comp16_1_eq, comp16_1_less, comp16_1_more, comp16_2_eq, comp16_2_less,
       comp16_2_more;

  COMP16 comp16_1 (.A(A[31:16]), .B(B[31:16]), .EQ(comp16_1_eq), .MORE(comp16_1_more), .LESS(comp16_1_less));
  COMP16 comp16_2 (.A(A[15:0]), .B(B[15:0]), .EQ(comp16_2_eq), .MORE(comp16_2_more), .LESS(comp16_2_less));
  and and_1 (EQ, comp16_1_eq, comp16_2_eq);
  and and_2 (and_2_out, comp16_1_eq, comp16_2_more);
  or or_1 (MORE, comp16_1_more, and_2_out);
  or or_2 (LESS, comp16_1_less, and_3_out);
  and and_3 (and_3_out, comp16_1_eq, comp16_2_less);
endmodule
